// Logisim project e2380863.circ as structural Verilog: 1 circuit, main circuit main
module main (
  input  O1,
  input  O0,
  input  S,
  input  A1,
  input  A0,
  input  B1,
  input  B0,
  output E,
  output G,
  output L,
  output B,
  output N,
  output L0,
  output L1,
  output L2,
  output L3,
  output L4,
  output L5,
  output L6,
  output L7
);

  wire and_1_out, and_2_out, and_3_out, and_4_out, and_5_out, and_6_out, and_7_out, and_11_out, and_14_out,
       and_15_out, n3_to_8_decoder_74138_1_p5, n3_to_8_decoder_74138_1_p7, n3_to_8_decoder_74138_1_p8,
       n3_to_8_decoder_74138_1_p9, n3_to_8_decoder_74138_1_p10, n3_to_8_decoder_74138_1_p11,
       n3_to_8_decoder_74138_1_p12, n3_to_8_decoder_74138_1_p13, n3_to_8_decoder_74138_1_p14,
       n4_to_1_mux_x2_74153_1_p13, n4_to_1_mux_x2_74153_1_p14, n4_to_1_mux_x2_74153_2_p9,
       n4_to_1_mux_x2_74153_3_p13, n4_to_1_mux_x2_74153_3_p14, n4_to_1_mux_x2_74153_4_p9,
       n4_to_1_mux_x2_74153_4_p11, n4_to_1_mux_x2_74153_4_p12, n4_to_1_mux_x2_74153_5_p6,
       n4_to_1_mux_x2_74153_5_p11, nor_1_out, nor_2_out, nor_3_out, not_1_out, not_2_out, not_3_out,
       not_4_out, not_5_out, not_6_out, not_7_out, not_8_out, not_9_out, not_10_out, not_11_out, or_1_out,
       or_2_out, or_3_out, or_4_out, or_5_out, xor_1_out, xor_2_out, xor_3_out;

  not not_1 (not_1_out, A1);
  not not_2 (not_2_out, A0);
  not not_3 (not_3_out, B1);
  not not_4 (not_4_out, B0);
  xor xor_1 (xor_1_out, A1, B1);
  xor xor_2 (xor_2_out, A0, B0);
  and and_1 (and_1_out, not_1_out, B1);
  and and_2 (and_2_out, not_2_out, B0);
  or or_1 (or_1_out, not_1_out, B1);
  not not_5 (not_5_out, 1'b1);
  not not_6 (not_6_out, 1'b1);
  not not_7 (not_7_out, 1'b1);
  not not_8 (not_8_out, 1'b1);
  // _4_to_1_MUX__x2___74153 #(.Facing("east")) 4_to_1_mux_x2_74153_1: pin names not known; wires that end beside it: not_8_out, not_8_out, not_8_out, 1'b1, not_8_out, 1'b1, 1'b1, not_8_out, not_8_out, B0, not_8_out, A0, n4_to_1_mux_x2_74153_1_p13, n4_to_1_mux_x2_74153_1_p14
  xor xor_3 (xor_3_out, A0, B0);
  and and_3 (and_3_out, A1, not_3_out);
  or or_2 (or_2_out, A0, not_4_out);
  and and_4 (and_4_out, not_1_out, B1);
  or or_3 (or_3_out, not_2_out, B0);
  not not_9 (not_9_out, 1'b1);
  nor nor_1 (nor_1_out, xor_1_out, xor_2_out);
  and and_5 (and_5_out, and_2_out, or_1_out);
  and and_6 (and_6_out, and_3_out, or_2_out);
  and and_7 (and_7_out, and_4_out, or_3_out);
  nor nor_2 (nor_2_out, O1, O0);
  or or_4 (or_4_out, and_1_out, and_5_out);
  // _4_to_1_MUX__x2___74153 #(.Facing("east")) 4_to_1_mux_x2_74153_2: pin names not known; wires that end beside it: A0, A1, not_5_out, not_5_out, not_5_out, B0, 1'b1, not_5_out, n4_to_1_mux_x2_74153_2_p9
  not not_10 (not_10_out, n4_to_1_mux_x2_74153_1_p13);
  or or_5 (or_5_out, and_6_out, and_7_out);
  nor nor_3 (nor_3_out, nor_1_out, or_4_out);
  not not_11 (not_11_out, O1);
  // _4_to_1_MUX__x2___74153 #(.Facing("east")) 4_to_1_mux_x2_74153_3: pin names not known; wires that end beside it: not_8_out, n4_to_1_mux_x2_74153_1_p13, n4_to_1_mux_x2_74153_1_p13, 1'b1, n4_to_1_mux_x2_74153_1_p13, not_10_out, not_10_out, n4_to_1_mux_x2_74153_1_p13, not_8_out, B1, not_8_out, A1, n4_to_1_mux_x2_74153_3_p13, n4_to_1_mux_x2_74153_3_p14
  and and_8 (E, nor_2_out, nor_1_out);
  and and_9 (L, nor_2_out, or_4_out);
  and and_10 (G, nor_2_out, nor_3_out);
  and and_11 (and_11_out, not_11_out, O0);
  and and_12 (B, and_11_out, n4_to_1_mux_x2_74153_2_p9);
  and and_13 (N, or_4_out, and_14_out);
  // _4_to_1_MUX__x2___74153 #(.Facing("east")) 4_to_1_mux_x2_74153_4: pin names not known; wires that end beside it: A1, not_7_out, n4_to_1_mux_x2_74153_1_p14, xor_3_out, not_6_out, A0, n4_to_1_mux_x2_74153_3_p14, or_5_out, n4_to_1_mux_x2_74153_4_p9, n4_to_1_mux_x2_74153_4_p9, n4_to_1_mux_x2_74153_4_p11, n4_to_1_mux_x2_74153_4_p12
  // _4_to_1_MUX__x2___74153 #(.Facing("east")) 4_to_1_mux_x2_74153_5: pin names not known; wires that end beside it: not_6_out, A1, n4_to_1_mux_x2_74153_3_p13, not_9_out, S, n4_to_1_mux_x2_74153_5_p6, S, O0, n4_to_1_mux_x2_74153_5_p6, O0, n4_to_1_mux_x2_74153_5_p11
  not not_12 (n4_to_1_mux_x2_74153_4_p9, 1'b1);
  not not_13 (n4_to_1_mux_x2_74153_5_p6, 1'b1);
  and and_14 (and_14_out, S, and_15_out);
  and and_15 (and_15_out, O0, O1);
  // _3_to_8_decoder__74138 #(.Facing("east")) 3_to_8_decoder_74138_1: pin names not known; wires that end beside it: n4_to_1_mux_x2_74153_4_p11, n4_to_1_mux_x2_74153_4_p12, n4_to_1_mux_x2_74153_5_p11, O1, n3_to_8_decoder_74138_1_p5, n3_to_8_decoder_74138_1_p5, n3_to_8_decoder_74138_1_p7, n3_to_8_decoder_74138_1_p8, n3_to_8_decoder_74138_1_p9, n3_to_8_decoder_74138_1_p10, n3_to_8_decoder_74138_1_p11, n3_to_8_decoder_74138_1_p12, n3_to_8_decoder_74138_1_p13, n3_to_8_decoder_74138_1_p14
  not not_14 (n3_to_8_decoder_74138_1_p5, O1);
  not not_15 (L0, n3_to_8_decoder_74138_1_p7);
  not not_16 (L2, n3_to_8_decoder_74138_1_p9);
  not not_17 (L4, n3_to_8_decoder_74138_1_p11);
  not not_18 (L6, n3_to_8_decoder_74138_1_p13);
  not not_19 (L1, n3_to_8_decoder_74138_1_p8);
  not not_20 (L3, n3_to_8_decoder_74138_1_p10);
  not not_21 (L5, n3_to_8_decoder_74138_1_p12);
  not not_22 (L7, n3_to_8_decoder_74138_1_p14);
endmodule
